# Fritzing sketch annoying_v1 (saved by Fritzing 0.9.4)
perfboards: 1

parts:
  Mod1 = Raspberry Pi Pico
  DFRobot_DFPlayer_Mini1 = DFRobot DFPlayer Mini [part_number=DFR0299]
  SP1 = SPEAKER [package=pcb_mount_speaker]
  IC1 = IC, DIP package, 8 pins [chip_label=IC]
  Q1 = Basic FET P-Channel [package="TO220 [THT]"]
  Q2 = Basic FET N-Channel [package="D2Pak [SMD]"]
  ZS-042_RTC1 = ZS-042 RTC Module
  R1 = Resistor [tolerance=±5% resistance=22k package=THT]
  R2 = Resistor [tolerance=±5% resistance=22k package=THT]
  R3 = Resistor [tolerance=±5% resistance=3k package=THT]
  C1 = Ceramic Capacitor [capacitance=100nF package="100 mil [THT, multilayer]"]
  R4 = Resistor [tolerance=±5% resistance=100k package=THT]
  R5 = Resistor [tolerance=±5% resistance=100k package=THT]

nets:
  N1: Mod1.pin_1, DFRobot_DFPlayer_Mini1.VCC, Q1.drain
  N2: Mod1.pin_2, DFRobot_DFPlayer_Mini1.RX
  N3: Mod1.pin_3, Mod1.pin_8, Mod1.pin_13, Mod1.pin_18, Mod1.pin_23, Mod1.pin_28, Mod1.pin_33, Mod1.pin_38, Mod1.pin_42, DFRobot_DFPlayer_Mini1.GND-1, DFRobot_DFPlayer_Mini1.GND-2, IC1.pin4, Q2.source, ZS-042_RTC1.GND, R2.Pin_1, C1.1
  N4: Mod1.pin_4, DFRobot_DFPlayer_Mini1.BUSY
  N5: Mod1.pin_21, ZS-042_RTC1.SDA
  N6: Mod1.pin_22, ZS-042_RTC1.SCL
  N7: Mod1.pin_26, Q2.Gate, R2.Pin_0
  N8: DFRobot_DFPlayer_Mini1.SPK_1, SP1.+
  N9: DFRobot_DFPlayer_Mini1.SPK_2, SP1.-
  N10: IC1.pin1, IC1.pin5, R4.Pin_0
  N11: IC1.pin2, ZS-042_RTC1.SQW, R3.Pin_0, C1.0
  N12: IC1.pin3, IC1.pin6, R5.Pin_1
  N13: IC1.pin7, Q2.drain, R1.Pin_0
  N14: IC1.pin8, Q1.source, ZS-042_RTC1.VCC, R1.Pin_1, R3.Pin_1, R4.Pin_1, R5.Pin_0

custom parts:
  Raspberry Pi Pico: Raspberry Pi Pico. Based around the RP2040 microcontroller the Pico is a low cost microcontroller device bringing Raspberry Pi quality, cost, and easy of use to the microcontroller space. Jan 2021, Split part in to two versions: tht (this one) and SMD. This one will drill holes for a .1 in header in pcb to allow plugging in the module as well as providing pads to solder the module to the top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
